// Logisim project 8Bit-PC-backup - Copy.circ as structural Verilog: 15 circuits, main circuit main
module main (
);

  wire ABinv, ACin, button_1_out, button_2_out, clock_1_clk, EEParg, EEPladr, flipflop_1_q, flipflop_2_q,
       IRI, JUMP, NOT_AEO_bec7f85f, NOT_EEPEO_2dfe95c8, NOT_EEwrite_42683ca5, NOT_PCEO_d757fd25,
       NOT_PCL_7825ed6a, NOT_RAMEO_8a4f1c54, NOT_RAMwrite_1c76035f, NOT_REOA_05b997d9, NOT_REOB_045ec1e2,
       PCCE, RAMladr, RLA, RLB;
  wire [7:0] eeprom_1_data, ireg_1_out, pc_1_pcout, ram_1_dout, reg_ab_1e8063b0_1_a_e_53ff4192,
       reg_ab_1e8063b0_1_out_a_d614a9c4, reg_ab_1e8063b0_1_out_b_577eee64;

  Button button_1 (.out(button_1_out));
  Clock clock_1 (.ClkHalt(flipflop_1_q), .ClkMan(flipflop_2_q), .Clk(clock_1_clk));
  FlipFlop flipflop_1 (.Q(flipflop_1_q), .toggle(button_1_out));
  FlipFlop flipflop_2 (.Q(flipflop_2_q), .toggle(button_2_out));
  Button button_2 (.out(button_2_out));
  RAM ram_1 (
    .Dout(ram_1_dout), .adr(reg_ab_1e8063b0_1_a_e_53ff4192), .Din(reg_ab_1e8063b0_1_a_e_53ff4192),
    .NOT_EO_36d354d6(NOT_RAMEO_8a4f1c54), .NOT_write_da732dde(NOT_RAMwrite_1c76035f), .LoadAdr(RAMladr));
  EEPROM eeprom_1 (
    .data(eeprom_1_data), .NOT_write_da732dde(NOT_EEwrite_42683ca5), .args(EEParg), .LoadAdr(EEPladr),
    .NOT_EO_36d354d6(NOT_EEPEO_2dfe95c8), .adr(eeprom_1_data), .in(eeprom_1_data));
  IReg ireg_1 (.Out(ireg_1_out), .LE(IRI), .In(eeprom_1_data));
  // Probe on eeprom_1_data
  ControllLogic controlllogic_1 (
    .PC_LOAD_I_b14deb23(NOT_PCL_7825ed6a), .RAM_ADR_I_9d97a65e(RAMladr), .EEPROM_ADR_I_9ecaf3d3(EEPladr),
    .REG_A_I_b7a9c98b(RLA), .REG_B_I_0682107d(RLB), .REG_INST_I_34505d7a(IRI),
    .RAM_WRITE_I_854caec8(NOT_RAMwrite_1c76035f), .EEPROM_WRITE_I_25019cab(NOT_EEwrite_42683ca5),
    .PC_INC_4603f465(PCCE), .ALU_Cin_b4b6776b(ACin), .ALU_Binv_c2f2766f(ABinv), .EEPROM_ARG_251898ab(EEParg),
    .JUMP(JUMP), .PC_O_8f4ee290(NOT_PCEO_d757fd25), .RAM_O_82bedc8d(NOT_RAMEO_8a4f1c54),
    .EEPROM_O_6c0ab249(NOT_EEPEO_2dfe95c8), .REG_A_O_0cb46501(NOT_REOA_05b997d9),
    .REG_B_O_b824fc97(NOT_REOB_045ec1e2), .ALU_O_bc04dd2d(NOT_AEO_bec7f85f), .Clk(clock_1_clk),
    .IREG(ireg_1_out));  // open: nc, out_25, out_9, out_10
  PC pc_1 (
    .PCout(pc_1_pcout), .LoadIn(pc_1_pcout), .CE(PCCE), .Clk(clock_1_clk),
    .NOT_load_3afa87d2(NOT_PCL_7825ed6a), .NOT_OE_5a23fa50(NOT_PCEO_d757fd25));
  Reg_AB_1e8063b0 reg_ab_1e8063b0_1 (
    .A_E_53ff4192(reg_ab_1e8063b0_1_a_e_53ff4192), .Out_A_d614a9c4(reg_ab_1e8063b0_1_out_a_d614a9c4),
    .B_E_8934d4ad(reg_ab_1e8063b0_1_a_e_53ff4192), .Out_B_577eee64(reg_ab_1e8063b0_1_out_b_577eee64),
    .LE_A_5db6e4e8(RLA), .LE_B_879dfcc8(RLB), .In(eeprom_1_data), .NOT_EOA_a7a08ba7(NOT_REOA_05b997d9),
    .NOT_OEB_606b30d0(NOT_REOB_045ec1e2));
  ALU_T_a1d61d21 alu_t_a1d61d21_1 (
    .out(pc_1_pcout), .Cin(ACin), .Binv(ABinv), .A(reg_ab_1e8063b0_1_out_a_d614a9c4),
    .B(reg_ab_1e8063b0_1_out_b_577eee64), .NOT_EO_36d354d6(NOT_AEO_bec7f85f));
endmodule

// Reg
module Reg_AB_1e8063b0 (
  input  LE_A_5db6e4e8,
  input  NOT_EOA_a7a08ba7,
  input  LE_B_879dfcc8,
  input  NOT_OEB_606b30d0,
  input  [7:0] In,
  output [7:0] A_E_53ff4192,
  output [7:0] Out_A_d614a9c4,
  output [7:0] B_E_8934d4ad,
  output [7:0] Out_B_577eee64
);

  DIP_74574 dip_74574_1 (
    .Q1(Out_A_d614a9c4[0]), .Q2(Out_A_d614a9c4[1]), .Q3(Out_A_d614a9c4[2]), .Q4(Out_A_d614a9c4[3]),
    .Q5(Out_A_d614a9c4[4]), .Q6(Out_A_d614a9c4[5]), .Q7(Out_A_d614a9c4[6]), .Q8(Out_A_d614a9c4[7]),
    .D1(In[0]), .D2(In[1]), .OE(1'b0), .D3(In[2]), .D4(In[3]), .D5(In[4]), .D6(In[5]), .D7(In[6]),
    .CLK(LE_A_5db6e4e8), .D8(In[7]));
  DIP_74574 dip_74574_2 (
    .Q1(Out_B_577eee64[0]), .Q2(Out_B_577eee64[1]), .Q3(Out_B_577eee64[2]), .Q4(Out_B_577eee64[3]),
    .Q5(Out_B_577eee64[4]), .Q6(Out_B_577eee64[5]), .Q7(Out_B_577eee64[6]), .Q8(Out_B_577eee64[7]),
    .D1(In[0]), .D2(In[1]), .OE(1'b0), .D3(In[2]), .D4(In[3]), .D5(In[4]), .D6(In[5]), .D7(In[6]),
    .CLK(LE_B_879dfcc8), .D8(In[7]));
  BusTranscever bustranscever_1 (
    .A(Out_A_d614a9c4), .B(A_E_53ff4192), .in_3(Out_A_d614a9c4), .in_4(A_E_53ff4192), .dir(1'b1),
    .NOT_OE(NOT_EOA_a7a08ba7));
  BusTranscever bustranscever_2 (
    .A(Out_B_577eee64), .B(B_E_8934d4ad), .in_3(Out_B_577eee64), .in_4(B_E_8934d4ad), .dir(1'b1),
    .NOT_OE(NOT_OEB_606b30d0));

  // Other names for the same wires on the sheet: NOT_EOB_7556ec8a = NOT_OEB_606b30d0
endmodule

module Display (
  input  [7:0] in_1
);

  Hex_Digit_Display hex_digit_display_1 (.value(in_1[3:0]), .dp(1'b0));
  Hex_Digit_Display hex_digit_display_2 (.value(in_1[7:4]), .dp(1'b0));
endmodule

module Clock (
  input  ClkHalt,
  input  ClkMan,
  output Clk
);

  wire and_1_out, clock_1_out, not_1_out;

  Clock_part clock_1 (.out(clock_1_out));
  and and_1 (and_1_out, clock_1_out, not_1_out);
  not not_1 (not_1_out, ClkHalt);
  or or_1 (Clk, and_1_out, ClkMan);
endmodule

module PC (
  input  Clk,
  input  NOT_load_3afa87d2,
  input  NOT_OE_5a23fa50,
  input  CE,
  input  [7:0] LoadIn,
  output [7:0] PCout
);

  wire dip_74163_1_tc;
  wire [3:0] dip_74163_1_q1, dip_74163_2_q1;

  DIP_74163 dip_74163_1 (
    .Q1(dip_74163_1_q1[0]), .Q2(dip_74163_1_q1[1]), .Q3(dip_74163_1_q1[2]), .Q4(dip_74163_1_q1[3]),
    .TC(dip_74163_1_tc), .LE(NOT_load_3afa87d2), .CEP(CE), .CET(CE), .CLK(Clk), .D1(LoadIn[0]),
    .D2(LoadIn[1]), .D3(LoadIn[2]), .CE(1'b0), .D4(LoadIn[3]));
  DIP_74163 dip_74163_2 (
    .Q1(dip_74163_2_q1[0]), .Q2(dip_74163_2_q1[1]), .Q3(dip_74163_2_q1[2]), .Q4(dip_74163_2_q1[3]),
    .LE(NOT_load_3afa87d2), .CEP(dip_74163_1_tc), .CET(dip_74163_1_tc), .CLK(Clk), .D1(LoadIn[4]),
    .D2(LoadIn[5]), .D3(LoadIn[6]), .CE(1'b0), .D4(LoadIn[7]));  // open: TC
  BusTranscever bustranscever_1 (
    .A(PCout), .B({dip_74163_2_q1, dip_74163_1_q1}), .in_3(PCout), .in_4({dip_74163_2_q1, dip_74163_1_q1}),
    .dir(1'b0), .NOT_OE(NOT_OE_5a23fa50));

  // Other names for the same wires on the sheet: NOT_EO_36d354d6 = NOT_OE_5a23fa50
endmodule

module RAM (
  input  LoadAdr,
  input  NOT_EO_36d354d6,
  input  NOT_write_da732dde,
  input  [7:0] adr,
  input  [7:0] Din,
  output [7:0] Dout
);

  wire button_1_out, EO, write;
  wire [7:0] dip_74574_1_q1;

  not not_1 (EO, NOT_EO_36d354d6);
  not not_2 (write, NOT_write_da732dde);
  DIP_74574 dip_74574_1 (
    .Q1(dip_74574_1_q1[0]), .Q2(dip_74574_1_q1[1]), .Q3(dip_74574_1_q1[2]), .Q4(dip_74574_1_q1[3]),
    .Q5(dip_74574_1_q1[4]), .Q6(dip_74574_1_q1[5]), .Q7(dip_74574_1_q1[6]), .Q8(dip_74574_1_q1[7]),
    .D1(adr[0]), .D2(adr[1]), .OE(1'b0), .D3(adr[2]), .D4(adr[3]), .D5(adr[4]), .D6(adr[5]), .D7(adr[6]),
    .CLK(LoadAdr), .D8(adr[7]));
  Button button_1 (.out(button_1_out));
  RAM_part ram_1 ();  // open: addr, we, oe, clk, din, dout

  // Other names for the same wires on the sheet: LE = LoadAdr
endmodule

module EEPROM (
  input  LoadAdr,
  input  NOT_EO_36d354d6,
  input  NOT_write_da732dde,
  input  args,
  input  [7:0] adr,
  input  [7:0] in,
  output [7:0] data
);

  wire button_1_out, EO, write;
  wire [7:0] dip_74574_1_q1;

  not not_1 (EO, NOT_EO_36d354d6);
  not not_2 (write, NOT_write_da732dde);
  DIP_74574 dip_74574_1 (
    .Q1(dip_74574_1_q1[0]), .Q2(dip_74574_1_q1[1]), .Q3(dip_74574_1_q1[2]), .Q4(dip_74574_1_q1[3]),
    .Q5(dip_74574_1_q1[4]), .Q6(dip_74574_1_q1[5]), .Q7(dip_74574_1_q1[6]), .Q8(dip_74574_1_q1[7]),
    .D1(adr[0]), .D2(adr[1]), .OE(1'b0), .D3(adr[2]), .D4(adr[3]), .D5(adr[4]), .D6(adr[5]), .D7(adr[6]),
    .CLK(LoadAdr), .D8(adr[7]));
  RAM_part #(.addrWidth(9)) ram_1 (
    .addr({args, dip_74574_1_q1}), .data(data), .sel(1'b1), .clk(write), .ld(EO), .clr(button_1_out));
  Button button_1 (.out(button_1_out));

  // Other names for the same wires on the sheet: LE = LoadAdr

  // Notes on the sheet:
  //   Args, der 2te speicherbereich für die Argumente der Befehle im ersten Speicherbereich
endmodule

module ALU (
  input  Binv,
  input  [7:0] A,
  input  Cin,
  input  [7:0] B,
  output [7:0] Y,
  output Cout
);

  wire B0, B1, B2, B3, B4, B5, B6, B7, Carry;

  DIP_74283 dip_74283_1 (
    .Y2(Y[1]), .Y3(Y[2]), .Y1(Y[0]), .Y4(Y[3]), .COUT(Carry), .B1(B0), .A2(A[1]), .CIN(Cin), .B2(B1),
    .A3(A[2]), .B3(B2), .A4(A[3]), .B4(B3), .A1(A[0]));
  DIP_74283 dip_74283_2 (
    .Y2(Y[5]), .Y3(Y[6]), .Y1(Y[4]), .Y4(Y[7]), .COUT(Cout), .B1(B4), .A2(A[5]), .CIN(Carry), .B2(B5),
    .A3(A[6]), .B3(B6), .A4(A[7]), .B4(B7), .A1(A[4]));
  DIP_7486 dip_7486_1 (
    .Y2(B1), .Y3(B2), .Y4(B3), .Y1(B0), .A2(Binv), .B2(B[1]), .A3(Binv), .A1(Binv), .B3(B[2]), .A4(Binv),
    .B4(B[3]), .B1(B[0]));
  DIP_7486 dip_7486_2 (
    .Y2(B5), .Y3(B6), .Y4(B7), .Y1(B4), .A2(Binv), .B2(B[5]), .A3(Binv), .A1(Binv), .B3(B[6]), .A4(Binv),
    .B4(B[7]), .B1(B[4]));

  // Other names for the same wires on the sheet: rB0 = B[0]; rB1 = B[1]; rB2 = B[2]; rB3 = B[3]; rB4 = B[4];
  //   rB5 = B[5]; rB6 = B[6]; rB7 = B[7]
endmodule

// 74LS245
module L_74_245_4198fcca (
  input  Dir,
  input  NOT_OE_5a23fa50,
  input  A1,
  input  in_4,
  input  in_5,
  input  in_6,
  input  A3,
  input  B3,
  input  A4,
  input  B4,
  input  A5,
  input  B5,
  input  in_13,
  input  B6,
  input  A7,
  input  B7,
  input  in_17,
  input  B8,
  output B1,
  output out_20,
  output B2,
  output A2,
  output out_23,
  output out_24,
  output out_25,
  output out_26,
  output out_27,
  output out_28,
  output out_29,
  output A6,
  output out_31,
  output out_32,
  output out_33,
  output A8
);

  wire and_1_out, and_2_out;

  and and_1 (and_1_out, Dir, ~NOT_OE_5a23fa50);  // AND_Gate
  assign B1 = and_1_out ? A1 : 1'bz;  // Controlled_Buffer controlled_buffer_1
  assign B2 = and_1_out ? in_5 : 1'bz;  // Controlled_Buffer controlled_buffer_2
  assign out_23 = and_1_out ? A3 : 1'bz;  // Controlled_Buffer controlled_buffer_3
  assign out_25 = and_1_out ? A4 : 1'bz;  // Controlled_Buffer controlled_buffer_4
  assign out_27 = and_1_out ? A5 : 1'bz;  // Controlled_Buffer controlled_buffer_5
  assign out_29 = and_1_out ? in_13 : 1'bz;  // Controlled_Buffer controlled_buffer_6
  assign out_31 = and_1_out ? A7 : 1'bz;  // Controlled_Buffer controlled_buffer_7
  assign out_33 = and_1_out ? in_17 : 1'bz;  // Controlled_Buffer controlled_buffer_8
  and and_2 (and_2_out, ~Dir, ~NOT_OE_5a23fa50);  // AND_Gate
  assign out_20 = and_2_out ? in_4 : 1'bz;  // Controlled_Buffer controlled_buffer_9
  assign A2 = and_2_out ? in_6 : 1'bz;  // Controlled_Buffer controlled_buffer_10
  assign out_24 = and_2_out ? B3 : 1'bz;  // Controlled_Buffer controlled_buffer_11
  assign out_26 = and_2_out ? B4 : 1'bz;  // Controlled_Buffer controlled_buffer_12
  assign out_28 = and_2_out ? B5 : 1'bz;  // Controlled_Buffer controlled_buffer_13
  assign A6 = and_2_out ? B6 : 1'bz;  // Controlled_Buffer controlled_buffer_14
  assign out_32 = and_2_out ? B7 : 1'bz;  // Controlled_Buffer controlled_buffer_15
  assign A8 = and_2_out ? B8 : 1'bz;  // Controlled_Buffer controlled_buffer_16
endmodule

// BusT
module BusTranscever (
  input  NOT_OE,
  input  dir,
  input  [7:0] in_3,
  input  [7:0] in_4,
  output [7:0] A,
  output [7:0] B
);

  wire DIR_AND_NOE, NDIR_AND_NOE, NOT_dir, OE;
  wire [7:0] controlled_buffer_1_out, l_74_245_4198fcca_1_b1;

  not not_1 (OE, NOT_OE);
  not not_2 (NOT_dir, dir);
  assign controlled_buffer_1_out = dir ? in_3 : 8'bz;  // Controlled_Buffer controlled_buffer_1
  assign A = DIR_AND_NOE ? controlled_buffer_1_out : 8'bz;  // Controlled_Buffer controlled_buffer_2
  L_74_245_4198fcca l_74_245_4198fcca_1 (
    .out_20(controlled_buffer_1_out[0]), .A2(controlled_buffer_1_out[1]),
    .out_24(controlled_buffer_1_out[2]), .out_26(controlled_buffer_1_out[3]),
    .out_28(controlled_buffer_1_out[4]), .A6(controlled_buffer_1_out[5]),
    .out_32(controlled_buffer_1_out[6]), .A8(controlled_buffer_1_out[7]), .B1(l_74_245_4198fcca_1_b1[0]),
    .B2(l_74_245_4198fcca_1_b1[1]), .out_23(l_74_245_4198fcca_1_b1[2]), .out_25(l_74_245_4198fcca_1_b1[3]),
    .out_27(l_74_245_4198fcca_1_b1[4]), .out_29(l_74_245_4198fcca_1_b1[5]),
    .out_31(l_74_245_4198fcca_1_b1[6]), .out_33(l_74_245_4198fcca_1_b1[7]), .Dir(dir),
    .A1(controlled_buffer_1_out[0]), .in_5(controlled_buffer_1_out[1]), .A3(controlled_buffer_1_out[2]),
    .A4(controlled_buffer_1_out[3]), .A5(controlled_buffer_1_out[4]), .in_13(controlled_buffer_1_out[5]),
    .A7(controlled_buffer_1_out[6]), .in_17(controlled_buffer_1_out[7]), .NOT_OE_5a23fa50(NOT_OE),
    .in_4(l_74_245_4198fcca_1_b1[0]), .in_6(l_74_245_4198fcca_1_b1[1]), .B3(l_74_245_4198fcca_1_b1[2]),
    .B4(l_74_245_4198fcca_1_b1[3]), .B5(l_74_245_4198fcca_1_b1[4]), .B6(l_74_245_4198fcca_1_b1[5]),
    .B7(l_74_245_4198fcca_1_b1[6]), .B8(l_74_245_4198fcca_1_b1[7]));
  assign l_74_245_4198fcca_1_b1 = NOT_dir ? in_4 : 8'bz;  // Controlled_Buffer controlled_buffer_3
  and and_1 (NDIR_AND_NOE, OE, dir);
  and and_2 (DIR_AND_NOE, OE, NOT_dir);
  assign B = NDIR_AND_NOE ? l_74_245_4198fcca_1_b1 : 8'bz;  // Controlled_Buffer controlled_buffer_4
endmodule

// ALU
module ALU_T_a1d61d21 (
  input  NOT_EO_36d354d6,
  input  Cin,
  input  Binv,
  input  [7:0] A,
  input  [7:0] B,
  output [7:0] out
);

  wire [7:0] bustranscever_1_b;

  BusTranscever bustranscever_1 (
    .A(out), .B(bustranscever_1_b), .in_3(out), .in_4(bustranscever_1_b), .dir(1'b0), .NOT_OE(NOT_EO_36d354d6));
  ALU alu_1 (.Y(bustranscever_1_b), .A(A), .Binv(Binv), .Cin(Cin), .B(B));  // open: Cout
endmodule

// T-FF
module FlipFlop (
  input  toggle,
  output Q
);

  J_K_Flip_Flop j_k_ff_1 (.J(toggle), .clk(toggle), .K(toggle), .Q(Q));  // open: Qn, preset, reset
endmodule

module InstReg (
  input  NOT_OE_5a23fa50,
  input  LE,
  input  [7:0] In,
  output [7:0] Out_A_d614a9c4
);

  DIP_74573 dip_74573_1 (
    .Q1(Out_A_d614a9c4[0]), .Q2(Out_A_d614a9c4[1]), .Q3(Out_A_d614a9c4[2]), .Q4(Out_A_d614a9c4[3]),
    .Q5(Out_A_d614a9c4[4]), .Q6(Out_A_d614a9c4[5]), .Q7(Out_A_d614a9c4[6]), .Q8(Out_A_d614a9c4[7]),
    .D1(In[0]), .D2(In[1]), .OE(NOT_OE_5a23fa50), .D3(In[2]), .D4(In[3]), .D5(In[4]), .D6(In[5]), .D7(In[6]),
    .LE(LE), .D8(In[7]));
endmodule

// IREG
module IReg (
  input  LE,
  input  [7:0] In,
  output [7:0] Out
);

  DIP_74574 dip_74574_1 (
    .Q1(Out[0]), .Q2(Out[1]), .Q3(Out[2]), .Q4(Out[3]), .Q5(Out[4]), .Q6(Out[5]), .Q7(Out[6]), .Q8(Out[7]),
    .D1(In[0]), .D2(In[1]), .OE(1'b0), .D3(In[2]), .D4(In[3]), .D5(In[4]), .D6(In[5]), .D7(In[6]), .CLK(LE),
    .D8(In[7]));

  // Notes on the sheet:
  //   Durchlässiger 573er für register unbrauchbar, muss 574 sein, getakted
endmodule

// Instruction Logic
module ControllLogic (
  input  [7:0] IREG,
  input  Clk,
  output PC_O_8f4ee290,
  output RAM_O_82bedc8d,
  output EEPROM_O_6c0ab249,
  output REG_A_O_0cb46501,
  output REG_B_O_b824fc97,
  output ALU_O_bc04dd2d,
  output out_9,
  output out_10,
  output PC_LOAD_I_b14deb23,
  output RAM_ADR_I_9d97a65e,
  output EEPROM_ADR_I_9ecaf3d3,
  output REG_A_I_b7a9c98b,
  output REG_B_I_0682107d,
  output REG_INST_I_34505d7a,
  output RAM_WRITE_I_854caec8,
  output EEPROM_WRITE_I_25019cab,
  output PC_INC_4603f465,
  output ALU_Cin_b4b6776b,
  output ALU_Binv_c2f2766f,
  output EEPROM_ARG_251898ab,
  output JUMP,
  output nc,
  output out_25
);

  wire button_1_out, button_2_out, dip_74138_2_y1, dip_74138_2_y2, dip_74138_2_y3, dip_74138_2_y4,
       dip_74138_2_y5, EEPAI, EEPWI, not_6_out, PCLI, RAMAI, RAMWI, REGAI, REGBI, REGII;
  wire [3:0] Istep;
  wire [7:0] H_sig_8efe3728;
  wire [7:7] IndipendentSig;

  DIP_74163 dip_74163_1 (
    .Q1(Istep[0]), .Q2(Istep[1]), .Q3(Istep[2]), .Q4(Istep[3]), .LE(1'b1), .CEP(1'b1), .CET(1'b1), .CLK(Clk),
    .D1(1'b0), .D2(1'b0), .D3(1'b0), .CE(IndipendentSig[7]), .D4(1'b0));  // open: TC
  DIP_74138 dip_74138_1 (
    .Y0(PC_O_8f4ee290), .Y1(RAM_O_82bedc8d), .Y2(EEPROM_O_6c0ab249), .Y3(REG_A_O_0cb46501),
    .Y4(REG_B_O_b824fc97), .Y5(ALU_O_bc04dd2d), .Y6(out_9), .Y7(out_10), .A0(H_sig_8efe3728[0]),
    .A1(H_sig_8efe3728[1]), .OE1(1'b0), .in_5(1'b0), .OE2(H_sig_8efe3728[3]), .A2(H_sig_8efe3728[2]));
  DIP_74138 dip_74138_2 (
    .Y0(PCLI), .Y1(dip_74138_2_y1), .Y2(dip_74138_2_y2), .Y3(dip_74138_2_y3), .Y4(dip_74138_2_y4),
    .Y5(dip_74138_2_y5), .Y6(RAMWI), .Y7(EEPWI), .A0(H_sig_8efe3728[4]), .A1(H_sig_8efe3728[5]), .OE1(1'b0),
    .in_5(1'b0), .OE2(H_sig_8efe3728[7]), .A2(H_sig_8efe3728[6]));
  RAM_part #(.addrWidth(12)) ram_1 (
    .addr({IREG, Istep}), .data(H_sig_8efe3728), .sel(1'b1), .clk(1'b0), .ld(1'b1), .clr(button_1_out));
  Button button_1 (.out(button_1_out));
  not not_1 (RAMAI, dip_74138_2_y1);
  not not_2 (EEPAI, dip_74138_2_y2);
  not not_3 (REGAI, dip_74138_2_y3);
  not not_4 (REGBI, dip_74138_2_y4);
  not not_5 (REGII, dip_74138_2_y5);
  RAM_part #(.addrWidth(12)) ram_2 (
    .addr({IREG, Istep}),
    .data({IndipendentSig[7], out_25, nc, JUMP, EEPROM_ARG_251898ab, ALU_Binv_c2f2766f, ALU_Cin_b4b6776b, PC_INC_4603f465}),
    .sel(1'b1), .clk(1'b0), .ld(1'b1), .clr(button_2_out));
  Button button_2 (.out(button_2_out));
  DIP_7408 dip_7408_1 (
    .Y2(EEPROM_ADR_I_9ecaf3d3), .Y3(REG_B_I_0682107d), .Y4(REG_A_I_b7a9c98b), .Y1(RAM_ADR_I_9d97a65e),
    .A2(Clk), .B2(EEPAI), .A3(Clk), .A1(Clk), .B3(REGBI), .A4(REGAI), .B4(Clk), .B1(RAMAI));
  DIP_7408 dip_7408_2 (
    .Y1(REG_INST_I_34505d7a), .A2(Clk), .A1(Clk), .B3(Clk), .B4(Clk), .B1(REGII));  // open: Y2, Y3, Y4, B2, A3, A4
  not not_6 (not_6_out, Clk);
  DIP_7432 dip_7432_1 (
    .Y2(RAM_WRITE_I_854caec8), .Y4(EEPROM_WRITE_I_25019cab), .Y1(PC_LOAD_I_b14deb23), .A2(not_6_out),
    .B2(RAMWI), .A1(not_6_out), .B3(not_6_out), .A4(EEPWI), .B4(not_6_out), .B1(PCLI));  // open: Y3, A3

  // Other names for the same wires on the sheet: Iadr[7:0] = IREG; EEPAI_d43e3928 = EEPROM_ADR_I_9ecaf3d3;
  //   EEPWI_957e0d5b = EEPROM_WRITE_I_25019cab; outSignalsDec[2:0] = H_sig_8efe3728[2:0];
  //   out_Enable_47d8fc43 = H_sig_8efe3728[3]; in_Enable_6b4e504d = H_sig_8efe3728[7];
  //   IndipendentSig[6:0] = {out_25, nc, JUMP, EEPROM_ARG_251898ab, ALU_Binv_c2f2766f, ALU_Cin_b4b6776b, PC_INC_4603f465};
  //   L_Sig_88618042[7:0] = {IndipendentSig[7], out_25, nc, JUMP, EEPROM_ARG_251898ab, ALU_Binv_c2f2766f, ALU_Cin_b4b6776b, PC_INC_4603f465};
  //   stepReset = IndipendentSig[7]; inSignalsDec[2:0] = H_sig_8efe3728[6:4]; PCLI_e275a15e = PC_LOAD_I_b14deb23;
  //   RAMAI_def62843 = RAM_ADR_I_9d97a65e; RAMWI_5f7c5aa9 = RAM_WRITE_I_854caec8; REGAI_b446f61a = REG_A_I_b7a9c98b;
  //   REGBI_19bccb02 = REG_B_I_0682107d; REGII_ac732675 = REG_INST_I_34505d7a

  // Notes on the sheet:
  //   Clock, für synchrones laden der Werte
endmodule
