// Logisim project 8Bit_PC_EVOLUTION_Backup2.circ as structural Verilog: 15 circuits, main circuit main
module main (
);

  wire ABinv, ACin, button_1_out, button_2_out, clock_1_clk, EEParg, EEPladr, flipflop_1_q, flipflop_2_q,
       IRI, JUMP, NOT_AEO, NOT_EEPEO, NOT_EEwrite, NOT_PCEO, NOT_PCL, NOT_RAEO, NOT_RAMEO, NOT_RAMwrite,
       NOT_REOB, PCCE, RAMladr, RLA, RLB;
  wire [7:0] eeprom_1_data, ireg_1_out, reg_ab_1e8063b0_1_out_a, reg_ab_1e8063b0_1_out_b;

  EEPROM eeprom_1 (
    .data(eeprom_1_data), .adr(eeprom_1_data), .NOT_write(NOT_EEwrite), .args(EEParg), .LoadAdr(EEPladr),
    .NOT_EO(NOT_EEPEO), .in(eeprom_1_data));
  Clock clock_1 (.ClkHalt(flipflop_1_q), .ClkMan(flipflop_2_q), .Clk(clock_1_clk));
  FlipFlop flipflop_1 (.Q(flipflop_1_q), .toggle(button_1_out));
  Button button_1 (.out(button_1_out));
  RAM ram_1 (
    .Dout(eeprom_1_data), .adr(eeprom_1_data), .NOT_EO(NOT_RAMEO), .NOT_write(NOT_RAMwrite),
    .LoadAdr(RAMladr), .Din(eeprom_1_data));
  IReg ireg_1 (.Out(ireg_1_out), .LE(IRI), .In(eeprom_1_data));
  Button button_2 (.out(button_2_out));
  FlipFlop flipflop_2 (.Q(flipflop_2_q), .toggle(button_2_out));
  // Probe on eeprom_1_data
  ControllLogic controlllogic_1 (
    .PC_LOAD_I(NOT_PCL), .RAM_ADR_I(RAMladr), .EEPROM_ADR_I(EEPladr), .REG_A_I(RLA), .REG_B_I(RLB),
    .REG_INST_I(IRI), .RAM_WRITE_I(NOT_RAMwrite), .EEPROM_WRITE_I(NOT_EEwrite), .PC_O(NOT_PCEO),
    .RAM_O(NOT_RAMEO), .EEPROM_O(NOT_EEPEO), .REG_A_O(NOT_RAEO), .REG_B_O(NOT_REOB), .ALU_O(NOT_AEO),
    .PC_INC(PCCE), .ALU_Cin(ACin), .ALU_Binv(ABinv), .EEPROM_ARG(EEParg), .JUMP(JUMP), .Clk(clock_1_clk),
    .IREG(ireg_1_out));  // open: out_17, out_18, out_25, nc
  PC pc_1 (
    .PCout(eeprom_1_data), .LoadIn(eeprom_1_data), .CE(PCCE), .Clk(clock_1_clk), .NOT_load(NOT_PCL),
    .NOT_OE(NOT_PCEO));
  ALU_T_a1d61d21 alu_t_a1d61d21_1 (
    .out(eeprom_1_data), .Cin(ACin), .Binv(ABinv), .A(reg_ab_1e8063b0_1_out_a), .B(reg_ab_1e8063b0_1_out_b),
    .NOT_EO_36d354d6(NOT_AEO));
  Reg_AB_1e8063b0 reg_ab_1e8063b0_1 (
    .A_E(eeprom_1_data), .Out_A(reg_ab_1e8063b0_1_out_a), .B_E(eeprom_1_data),
    .Out_B(reg_ab_1e8063b0_1_out_b), .LE_A(RLA), .LE_B(RLB), .In(eeprom_1_data), .NOT_EOA(NOT_RAEO),
    .NOT_OEB(NOT_REOB));
endmodule

// Reg
module Reg_AB_1e8063b0 (
  input  LE_A,
  input  NOT_EOA,
  input  LE_B,
  input  NOT_OEB,
  input  [7:0] In,
  output [7:0] A_E,
  output [7:0] Out_A,
  output [7:0] B_E,
  output [7:0] Out_B
);

  DIP_74574 dip_74574_1 (
    .Q1(Out_A[0]), .Q2(Out_A[1]), .Q3(Out_A[2]), .Q4(Out_A[3]), .Q5(Out_A[4]), .Q6(Out_A[5]), .Q7(Out_A[6]),
    .Q8(Out_A[7]), .D1(In[0]), .D2(In[1]), .OE(1'b0), .D3(In[2]), .D4(In[3]), .D5(In[4]), .D6(In[5]),
    .D7(In[6]), .CLK(LE_A), .D8(In[7]));
  DIP_74574 dip_74574_2 (
    .Q1(Out_B[0]), .Q2(Out_B[1]), .Q3(Out_B[2]), .Q4(Out_B[3]), .Q5(Out_B[4]), .Q6(Out_B[5]), .Q7(Out_B[6]),
    .Q8(Out_B[7]), .D1(In[0]), .D2(In[1]), .OE(1'b0), .D3(In[2]), .D4(In[3]), .D5(In[4]), .D6(In[5]),
    .D7(In[6]), .CLK(LE_B), .D8(In[7]));
  BusTranscever bustranscever_1 (.A(Out_A), .B(A_E), .in_3(Out_A), .in_4(A_E), .dir(1'b1), .NOT_OE(NOT_EOA));
  BusTranscever bustranscever_2 (.A(Out_B), .B(B_E), .in_3(Out_B), .in_4(B_E), .dir(1'b1), .NOT_OE(NOT_OEB));

  // Other names for the same wires on the sheet: NOT_EOB = NOT_OEB
endmodule

module Display (
  input  [7:0] in_1
);

  Hex_Digit_Display hex_digit_display_1 (.value(in_1[3:0]), .dp(1'b0));
  Hex_Digit_Display hex_digit_display_2 (.value(in_1[7:4]), .dp(1'b0));
endmodule

module Clock (
  input  ClkHalt,
  input  ClkMan,
  output Clk
);

  wire and_1_out, clock_1_out, not_1_out;

  Clock_part clock_1 (.out(clock_1_out));
  and and_1 (and_1_out, clock_1_out, not_1_out);
  not not_1 (not_1_out, ClkHalt);
  or or_1 (Clk, and_1_out, ClkMan);
endmodule

module PC (
  input  Clk,
  input  NOT_load,
  input  NOT_OE,
  input  CE,
  input  [7:0] LoadIn,
  output [7:0] PCout
);

  wire dip_74163_1_tc;
  wire [3:0] dip_74163_1_q1, dip_74163_2_q1;

  DIP_74163 dip_74163_1 (
    .Q1(dip_74163_1_q1[0]), .Q2(dip_74163_1_q1[1]), .Q3(dip_74163_1_q1[2]), .Q4(dip_74163_1_q1[3]),
    .TC(dip_74163_1_tc), .LE(NOT_load), .CEP(CE), .CET(CE), .CLK(Clk), .D1(LoadIn[0]), .D2(LoadIn[1]),
    .D3(LoadIn[2]), .CE(1'b0), .D4(LoadIn[3]));
  DIP_74163 dip_74163_2 (
    .Q1(dip_74163_2_q1[0]), .Q2(dip_74163_2_q1[1]), .Q3(dip_74163_2_q1[2]), .Q4(dip_74163_2_q1[3]),
    .LE(NOT_load), .CEP(dip_74163_1_tc), .CET(dip_74163_1_tc), .CLK(Clk), .D1(LoadIn[4]), .D2(LoadIn[5]),
    .D3(LoadIn[6]), .CE(1'b0), .D4(LoadIn[7]));  // open: TC
  BusTranscever bustranscever_1 (
    .A(PCout), .B({dip_74163_2_q1, dip_74163_1_q1}), .in_3(PCout), .in_4({dip_74163_2_q1, dip_74163_1_q1}),
    .dir(1'b0), .NOT_OE(NOT_OE));

  // Other names for the same wires on the sheet: NOT_EO = NOT_OE
endmodule

module RAM (
  input  LoadAdr,
  input  NOT_EO,
  input  NOT_write,
  input  [7:0] adr,
  input  [7:0] Din,
  output [7:0] Dout
);

  wire EO, write;
  wire [7:0] dip_74574_1_q1;

  not not_1 (EO, NOT_EO);
  not not_2 (write, NOT_write);
  DIP_74574 dip_74574_1 (
    .Q1(dip_74574_1_q1[0]), .Q2(dip_74574_1_q1[1]), .Q3(dip_74574_1_q1[2]), .Q4(dip_74574_1_q1[3]),
    .Q5(dip_74574_1_q1[4]), .Q6(dip_74574_1_q1[5]), .Q7(dip_74574_1_q1[6]), .Q8(dip_74574_1_q1[7]),
    .D1(adr[0]), .D2(adr[1]), .OE(1'b0), .D3(adr[2]), .D4(adr[3]), .D5(adr[4]), .D6(adr[5]), .D7(adr[6]),
    .CLK(LoadAdr), .D8(adr[7]));
  RAM_part ram_1 (.addr(dip_74574_1_q1), .we(write), .oe(EO), .clk(write), .din(Din), .dout(Dout));

  // Other names for the same wires on the sheet: LE = LoadAdr
endmodule

module EEPROM (
  input  LoadAdr,
  input  NOT_EO,
  input  NOT_write,
  input  args,
  input  [7:0] adr,
  input  [7:0] in,
  output [7:0] data
);

  wire EO, write;
  wire [7:0] dip_74574_1_q1;

  not not_1 (EO, NOT_EO);
  not not_2 (write, NOT_write);
  DIP_74574 dip_74574_1 (
    .Q1(dip_74574_1_q1[0]), .Q2(dip_74574_1_q1[1]), .Q3(dip_74574_1_q1[2]), .Q4(dip_74574_1_q1[3]),
    .Q5(dip_74574_1_q1[4]), .Q6(dip_74574_1_q1[5]), .Q7(dip_74574_1_q1[6]), .Q8(dip_74574_1_q1[7]),
    .D1(adr[0]), .D2(adr[1]), .OE(1'b0), .D3(adr[2]), .D4(adr[3]), .D5(adr[4]), .D6(adr[5]), .D7(adr[6]),
    .CLK(LoadAdr), .D8(adr[7]));
  RAM_part #(.addrWidth(9)) ram_1 (
    .addr({args, dip_74574_1_q1}), .we(write), .oe(EO), .clk(write), .din(in), .dout(data));

  // Other names for the same wires on the sheet: LE = LoadAdr

  // Notes on the sheet:
  //   Args, der 2te speicherbereich für die Argumente der Befehle im ersten Speicherbereich
endmodule

module ALU (
  input  Binv,
  input  [7:0] A,
  input  Cin,
  input  [7:0] B,
  output [7:0] Y,
  output Cout
);

  wire B0, B1, B2, B3, B4, B5, B6, B7, Carry;

  DIP_74283 dip_74283_1 (
    .Y2(Y[1]), .Y3(Y[2]), .Y1(Y[0]), .Y4(Y[3]), .COUT(Carry), .B1(B0), .A2(A[1]), .CIN(Cin), .B2(B1),
    .A3(A[2]), .B3(B2), .A4(A[3]), .B4(B3), .A1(A[0]));
  DIP_74283 dip_74283_2 (
    .Y2(Y[5]), .Y3(Y[6]), .Y1(Y[4]), .Y4(Y[7]), .COUT(Cout), .B1(B4), .A2(A[5]), .CIN(Carry), .B2(B5),
    .A3(A[6]), .B3(B6), .A4(A[7]), .B4(B7), .A1(A[4]));
  DIP_7486 dip_7486_1 (
    .Y2(B1), .Y3(B2), .Y4(B3), .Y1(B0), .A2(Binv), .B2(B[1]), .A3(Binv), .A1(Binv), .B3(B[2]), .A4(Binv),
    .B4(B[3]), .B1(B[0]));
  DIP_7486 dip_7486_2 (
    .Y2(B5), .Y3(B6), .Y4(B7), .Y1(B4), .A2(Binv), .B2(B[5]), .A3(Binv), .A1(Binv), .B3(B[6]), .A4(Binv),
    .B4(B[7]), .B1(B[4]));

  // Other names for the same wires on the sheet: rB0 = B[0]; rB1 = B[1]; rB2 = B[2]; rB3 = B[3]; rB4 = B[4];
  //   rB5 = B[5]; rB6 = B[6]; rB7 = B[7]
endmodule

// 74LS245
module L_74_245_4198fcca (
  input  Dir,
  input  NOT_OE_5a23fa50,
  input  A1,
  input  in_4,
  input  in_5,
  input  in_6,
  input  A3,
  input  B3,
  input  A4,
  input  B4,
  input  A5,
  input  B5,
  input  in_13,
  input  B6,
  input  A7,
  input  B7,
  input  in_17,
  input  B8,
  output B1,
  output out_20,
  output B2,
  output A2,
  output out_23,
  output out_24,
  output out_25,
  output out_26,
  output out_27,
  output out_28,
  output out_29,
  output A6,
  output out_31,
  output out_32,
  output out_33,
  output A8
);

  wire and_1_out, and_2_out;

  and and_1 (and_1_out, Dir, ~NOT_OE_5a23fa50);  // AND_Gate
  assign B1 = and_1_out ? A1 : 1'bz;  // Controlled_Buffer controlled_buffer_1
  assign B2 = and_1_out ? in_5 : 1'bz;  // Controlled_Buffer controlled_buffer_2
  assign out_23 = and_1_out ? A3 : 1'bz;  // Controlled_Buffer controlled_buffer_3
  assign out_25 = and_1_out ? A4 : 1'bz;  // Controlled_Buffer controlled_buffer_4
  assign out_27 = and_1_out ? A5 : 1'bz;  // Controlled_Buffer controlled_buffer_5
  assign out_29 = and_1_out ? in_13 : 1'bz;  // Controlled_Buffer controlled_buffer_6
  assign out_31 = and_1_out ? A7 : 1'bz;  // Controlled_Buffer controlled_buffer_7
  assign out_33 = and_1_out ? in_17 : 1'bz;  // Controlled_Buffer controlled_buffer_8
  and and_2 (and_2_out, ~Dir, ~NOT_OE_5a23fa50);  // AND_Gate
  assign out_20 = and_2_out ? in_4 : 1'bz;  // Controlled_Buffer controlled_buffer_9
  assign A2 = and_2_out ? in_6 : 1'bz;  // Controlled_Buffer controlled_buffer_10
  assign out_24 = and_2_out ? B3 : 1'bz;  // Controlled_Buffer controlled_buffer_11
  assign out_26 = and_2_out ? B4 : 1'bz;  // Controlled_Buffer controlled_buffer_12
  assign out_28 = and_2_out ? B5 : 1'bz;  // Controlled_Buffer controlled_buffer_13
  assign A6 = and_2_out ? B6 : 1'bz;  // Controlled_Buffer controlled_buffer_14
  assign out_32 = and_2_out ? B7 : 1'bz;  // Controlled_Buffer controlled_buffer_15
  assign A8 = and_2_out ? B8 : 1'bz;  // Controlled_Buffer controlled_buffer_16
endmodule

// BusT
module BusTranscever (
  input  NOT_OE,
  input  dir,
  input  [7:0] in_3,
  input  [7:0] in_4,
  output [7:0] A,
  output [7:0] B
);

  wire DIR_AND_NOE, NDIR_AND_NOE, NOT_dir, OE;
  wire [7:0] controlled_buffer_1_out, l_74_245_4198fcca_1_b1;

  not not_1 (OE, NOT_OE);
  not not_2 (NOT_dir, dir);
  assign controlled_buffer_1_out = dir ? in_3 : 8'bz;  // Controlled_Buffer controlled_buffer_1
  assign A = DIR_AND_NOE ? controlled_buffer_1_out : 8'bz;  // Controlled_Buffer controlled_buffer_2
  L_74_245_4198fcca l_74_245_4198fcca_1 (
    .out_20(controlled_buffer_1_out[0]), .A2(controlled_buffer_1_out[1]),
    .out_24(controlled_buffer_1_out[2]), .out_26(controlled_buffer_1_out[3]),
    .out_28(controlled_buffer_1_out[4]), .A6(controlled_buffer_1_out[5]),
    .out_32(controlled_buffer_1_out[6]), .A8(controlled_buffer_1_out[7]), .B1(l_74_245_4198fcca_1_b1[0]),
    .B2(l_74_245_4198fcca_1_b1[1]), .out_23(l_74_245_4198fcca_1_b1[2]), .out_25(l_74_245_4198fcca_1_b1[3]),
    .out_27(l_74_245_4198fcca_1_b1[4]), .out_29(l_74_245_4198fcca_1_b1[5]),
    .out_31(l_74_245_4198fcca_1_b1[6]), .out_33(l_74_245_4198fcca_1_b1[7]), .Dir(dir),
    .A1(controlled_buffer_1_out[0]), .in_5(controlled_buffer_1_out[1]), .A3(controlled_buffer_1_out[2]),
    .A4(controlled_buffer_1_out[3]), .A5(controlled_buffer_1_out[4]), .in_13(controlled_buffer_1_out[5]),
    .A7(controlled_buffer_1_out[6]), .in_17(controlled_buffer_1_out[7]), .NOT_OE_5a23fa50(NOT_OE),
    .in_4(l_74_245_4198fcca_1_b1[0]), .in_6(l_74_245_4198fcca_1_b1[1]), .B3(l_74_245_4198fcca_1_b1[2]),
    .B4(l_74_245_4198fcca_1_b1[3]), .B5(l_74_245_4198fcca_1_b1[4]), .B6(l_74_245_4198fcca_1_b1[5]),
    .B7(l_74_245_4198fcca_1_b1[6]), .B8(l_74_245_4198fcca_1_b1[7]));
  assign l_74_245_4198fcca_1_b1 = NOT_dir ? in_4 : 8'bz;  // Controlled_Buffer controlled_buffer_3
  and and_1 (NDIR_AND_NOE, OE, dir);
  and and_2 (DIR_AND_NOE, OE, NOT_dir);
  assign B = NDIR_AND_NOE ? l_74_245_4198fcca_1_b1 : 8'bz;  // Controlled_Buffer controlled_buffer_4
endmodule

// ALU
module ALU_T_a1d61d21 (
  input  NOT_EO_36d354d6,
  input  Cin,
  input  Binv,
  input  [7:0] A,
  input  [7:0] B,
  output [7:0] out
);

  wire [7:0] bustranscever_1_b;

  BusTranscever bustranscever_1 (
    .A(out), .B(bustranscever_1_b), .in_3(out), .in_4(bustranscever_1_b), .dir(1'b0), .NOT_OE(NOT_EO_36d354d6));
  ALU alu_1 (.Y(bustranscever_1_b), .A(A), .Binv(Binv), .Cin(Cin), .B(B));  // open: Cout
endmodule

// T-FF
module FlipFlop (
  input  toggle,
  output Q
);

  J_K_Flip_Flop j_k_ff_1 (.J(toggle), .K(toggle), .clk(toggle), .Q(Q));  // open: Qn, preset, reset
endmodule

module InstReg (
  input  NOT_OE_5a23fa50,
  input  LE,
  input  [7:0] In,
  output [7:0] Out_A_d614a9c4
);

  DIP_74573 dip_74573_1 (
    .Q1(Out_A_d614a9c4[0]), .Q2(Out_A_d614a9c4[1]), .Q3(Out_A_d614a9c4[2]), .Q4(Out_A_d614a9c4[3]),
    .Q5(Out_A_d614a9c4[4]), .Q6(Out_A_d614a9c4[5]), .Q7(Out_A_d614a9c4[6]), .Q8(Out_A_d614a9c4[7]),
    .D1(In[0]), .D2(In[1]), .OE(NOT_OE_5a23fa50), .D3(In[2]), .D4(In[3]), .D5(In[4]), .D6(In[5]), .D7(In[6]),
    .LE(LE), .D8(In[7]));
endmodule

// IREG
module IReg (
  input  LE,
  input  [7:0] In,
  output [7:0] Out
);

  DIP_74574 dip_74574_1 (
    .Q1(Out[0]), .Q2(Out[1]), .Q3(Out[2]), .Q4(Out[3]), .Q5(Out[4]), .Q6(Out[5]), .Q7(Out[6]), .Q8(Out[7]),
    .D1(In[0]), .D2(In[1]), .OE(1'b0), .D3(In[2]), .D4(In[3]), .D5(In[4]), .D6(In[5]), .D7(In[6]), .CLK(LE),
    .D8(In[7]));

  // Notes on the sheet:
  //   Durchlässiger 573er für register unbrauchbar, muss 574 sein, getakted
endmodule

// Instruction Logic
module ControllLogic (
  input  Clk,
  input  [7:0] IREG,
  output PC_LOAD_I,
  output RAM_ADR_I,
  output EEPROM_ADR_I,
  output REG_A_I,
  output REG_B_I,
  output REG_INST_I,
  output RAM_WRITE_I,
  output PC_O,
  output EEPROM_WRITE_I,
  output RAM_O,
  output EEPROM_O,
  output REG_A_O,
  output REG_B_O,
  output ALU_O,
  output out_17,
  output out_18,
  output PC_INC,
  output ALU_Cin,
  output ALU_Binv,
  output EEPROM_ARG,
  output JUMP,
  output nc,
  output out_25
);

  wire dip_74138_1_y1, dip_74138_1_y2, dip_74138_1_y3, dip_74138_1_y4, dip_74138_1_y5, EEPAI_I, EEPWI_I,
       not_6_out, PCLI_I, RAMAI_I, RAMWI_I, REGAI_I, REGBI_I, REGII_I;
  wire [3:0] I_MEM_ADD;
  wire [7:0] H_Inst;
  wire [7:7] IndipendentSig;

  DIP_74163 dip_74163_1 (
    .Q1(I_MEM_ADD[0]), .Q2(I_MEM_ADD[1]), .Q3(I_MEM_ADD[2]), .Q4(I_MEM_ADD[3]), .LE(1'b1), .CEP(1'b1),
    .CET(1'b1), .CLK(Clk), .D1(1'b0), .D2(1'b0), .D3(1'b0), .CE(IndipendentSig[7]), .D4(1'b0));  // open: TC
  DIP_74138 dip_74138_1 (
    .Y0(PCLI_I), .Y1(dip_74138_1_y1), .Y2(dip_74138_1_y2), .Y3(dip_74138_1_y3), .Y4(dip_74138_1_y4),
    .Y5(dip_74138_1_y5), .Y6(RAMWI_I), .Y7(EEPWI_I), .A0(H_Inst[4]), .A1(H_Inst[5]), .OE1(1'b0), .in_5(1'b0),
    .OE2(H_Inst[7]), .A2(H_Inst[6]));
  DIP_74138 dip_74138_2 (
    .Y0(PC_O), .Y1(RAM_O), .Y2(EEPROM_O), .Y3(REG_A_O), .Y4(REG_B_O), .Y5(ALU_O), .Y6(out_17), .Y7(out_18),
    .A0(H_Inst[0]), .A1(H_Inst[1]), .OE1(1'b0), .in_5(1'b0), .OE2(H_Inst[3]), .A2(H_Inst[2]));
  not not_1 (RAMAI_I, dip_74138_1_y1);
  not not_2 (EEPAI_I, dip_74138_1_y2);
  not not_3 (REGAI_I, dip_74138_1_y3);
  not not_4 (REGBI_I, dip_74138_1_y4);
  not not_5 (REGII_I, dip_74138_1_y5);
  ROM #(.addrWidth(12)) rom_1 (.addr({IREG, I_MEM_ADD}), .data(H_Inst));
  ROM #(.addrWidth(12)) rom_2 (
    .addr({IREG, I_MEM_ADD}),
    .data({IndipendentSig[7], out_25, nc, JUMP, EEPROM_ARG, ALU_Binv, ALU_Cin, PC_INC}));
  DIP_7408 dip_7408_1 (
    .Y2(EEPROM_ADR_I), .Y3(REG_B_I), .Y4(REG_A_I), .Y1(RAM_ADR_I), .A2(Clk), .B2(EEPAI_I), .A3(Clk),
    .A1(Clk), .B3(REGBI_I), .A4(REGAI_I), .B4(Clk), .B1(RAMAI_I));
  DIP_7408 dip_7408_2 (
    .Y1(REG_INST_I), .A2(Clk), .A1(Clk), .B3(Clk), .B4(Clk), .B1(REGII_I));  // open: Y2, Y3, Y4, B2, A3, A4
  not not_6 (not_6_out, Clk);
  DIP_7432 dip_7432_1 (
    .Y2(RAM_WRITE_I), .Y4(EEPROM_WRITE_I), .Y1(PC_LOAD_I), .A2(not_6_out), .B2(RAMWI_I), .A1(not_6_out),
    .B3(not_6_out), .A4(EEPWI_I), .B4(not_6_out), .B1(PCLI_I));  // open: Y3, A3

  // Other names for the same wires on the sheet: EEPAI = EEPROM_ADR_I; EEPWI = EEPROM_WRITE_I; out_Enable = H_Inst[3];
  //   in_Enable = H_Inst[7]; Istep[3:0] = I_MEM_ADD; I_MEM_ADD[11:4] = IREG; Iadr[7:0] = IREG;
  //   IndipendentSig[6:0] = {out_25, nc, JUMP, EEPROM_ARG, ALU_Binv, ALU_Cin, PC_INC};
  //   L_Inst[7:0] = {IndipendentSig[7], out_25, nc, JUMP, EEPROM_ARG, ALU_Binv, ALU_Cin, PC_INC};
  //   stepReset = IndipendentSig[7]; inSignalsDec[2:0] = H_Inst[6:4]; outSignalsDec[2:0] = H_Inst[2:0];
  //   PCLI = PC_LOAD_I; RAMAI = RAM_ADR_I; RAMWI = RAM_WRITE_I; REGAI = REG_A_I; REGBI = REG_B_I; REGII = REG_INST_I

  // Notes on the sheet:
  //   contents of rom_1 (hex, n*v repeats v):
  //   0 0 0 20 0 0 1 20 0 0 2 20 0 0 3 20 0 0 4 20 0 0 5 20 0 0 6 20 0 0 7 20 0 0 8 20 0 0 9 20 0 0 a 20 0
  //   0 b 20 0 0 c 20 0 0 d 20 0 0 e 20 0 0 f 20 0 0 10 20 0 0 11 20 0 0 12 20 0 0 13 20 0 0 14 20 0 0 15
  //   20 0 0 16 20 0 0 17 20 0 0 18 20 0 0 19 20 0 0 1a 20 0 0 1b 20 0 0 1c 20 84 1 1d 20 ff ff 1e 20 0 0
  //   1f 20 71 0 0 8 136*0 1 0 0 0 2 0 0 0 4 0 0 0 8 0 0 0 10 0 0 0 20 0 0 0 40 0 0 0 80 4*0 1 0 0 0 2 0 0
  //   0 4 0 0 0 8 0 0 0 10 0 0 0 20 0 0 0 40 0 0 0 80 4*0 1 0 0 0 2 0 0 0 4 0 0 0 8 0 0 0 10 0 0 0 20 0 0
  //   0 40 0 0 0 80 4*0 1 0 0 0 2 0 0 0 4 0 0 0 8 0 0 0 10 0 0 0 20 0 0 0 40 0 0 0 80 10 0 0 0 1d 0 0 0 2
  //   0 0 0 8 0 0 0 3 7*0 1 15*0 ff ff 0 0 60 0 0 0 20 7*0 e 0 0 14 4*0 c9 0 0 c 4*0 ce 0 0 c 4*0 95 0 0 c
  //   4*0 53 1 0 c 4*0 2 1 0 c 4*0 2e 1 0 c 4*0 71 0 0 8 4*0 81 1 0 8 4*0 68 0 d 8c 1 0 ad 31 1 0 e 20 b 0
  //   cd 15 4*0 6c 0 f 8c 8 0 cf 11 4*0 1 0 f 20 63 0 18 8c 69 0 8 8c 22 c0 8 3 64 0 19 8c 6c 0 f ac 6a 0
  //   18 ac 6b 0 19 ac 8 0 e0 3 6*0 bf af 1 0 bd 23 68 0 d 8c 1 0 ad 31 1 0 1 20 2 0 2d 14 4*0 3c 1 0 c
  //   4*0 ff ff bd 23 0 0 bf 8f 8 0 e0 3 6*0 bf af 1 0 b0 af 2 0 b1 af 3 0 bd 23 6c 0 e 8c 1a 0 e 10 8*0
  //   6a 0 10 8c 6b 0 11 8c 0 0 4 22 0 0 25 22 23 0 26 8e 25 1 0 c 8*0 ff ff 31 22 0 0 4 22 0 0 25 22 23 0
  //   26 8e ff ff 8 20 9 0 5 11 8*0 1e 1 0 c 8*0 6a 0 10 ac 6b 0 11 ac c3 0 0 8 8*0 6c 0 0 ac fd ff bd 23
  //   0 0 bf 8f 1 0 b0 8f 2 0 b1 8f 8 0 e0 3 6*0 8 50 68 0 8 ac 8 0 e0 3 8*0 66 0 8 8c 65 0 9 8c 68 0 a 8c
  //   f7 0 0 8 8*0 63 0 8 8c 1 0 8 21 dd 0 0 8 8*0 ff ff 8 21 e1 0 0 8 8*0 20 0 9 20 f9 ff 28 11 8*0 63 0
  //   8 ac ff 0 0 8 8*0 63 0 8 8c ff ff 8 21 ee 0 0 8 8*0 1 0 8 21 f3 0 0 8 8*0 67 0 9 8c fe ff 29 21 f8
  //   ff 28 11 8*0 63 0 8 ac ff 0 0 8 8*0 8 0 4b 31 da ff b 11 8*0 2 0 4b 31 e7 ff 2b 11 8*0 8 0 e0 3 10*0
  //   bf af 1 0 b0 af 2 0 b1 af 3 0 bd 23 67 0 10 8c 63 0 11 8c 0 0 6 20 0 0 24 22 64 0 5 8c 1e 1 0 c 10*0
  //   46 20 ff ff 31 22 ff ff 10 22 4 0 10 10 8*0 9 1 0 8 8*0 fd ff bd 23 0 0 bf 8f 1 0 b0 8f 2 0 b1 8f 8
  //   0 e0 3 8*0 43 0 88 8c 25 40 6 1 23 0 a8 ac 0 0 2 21 8 0 e0 3 8*0 ff ff 8 20 43 0 89 8c 22 40 9 1 24
  //   40 6 1 23 0 a8 ac 0 0 2 21 8 0 e0 3 10*0 8 20 1f 0 9 20 23 0 a 8d 0 0 a 55 1 0 8 21 4 0 28 11 8*0 30
  //   1 0 8 8*0 8 0 e0 3 8*0 70 0 8 8c 6f 0 1 8c 2b 8 1 1 10 0 1 10 4*0 1 0 8 21 70 0 8 ac 6d 0 9 8c 0 0 a
  //   20 4 0 9 10 4*0 fd ff 4a 21 6d 0 49 8d 45 1 0 8 4*0 1 0 a 20 63 0 b 8c 64 0 c 8c 0 0 2a ad ff ff 2b
  //   ad fe ff 2c ad 8 0 e0 3 6*0 bf af 1 0 bd 23 70 0 d 8c 0 0 e 20 0 0 1 20 23 0 2d 10 4*0 6d 0 cf 8d 0
  //   0 1 20 1c 0 2f 10 4*0 ff ff d8 21 6d 0 c 8f fe ff d8 21 6d 0 f 8f 23 0 eb 8d 0 0 84 21 0 0 e5 21 0 0
  //   66 21 25 1 0 c 6*0 1 20 6 0 2f 14 4*0 6d 0 c0 ad 70 0 19 8c ff ff 39 23 70 0 19 ac 79 1 0 8 4*0 ff
  //   ff ef 21 6d 0 f af 23 0 eb 8d 0 0 84 21 0 0 e5 21 0 0 66 21 1e 1 0 c 4*0 ff ff ad 21 3 0 ce 21 58 1
  //   0 8 4*0 ff ff bd 23 0 0 bf 8f 8 0 e0 3 4*0 81 1 0 8
  //   Clock, für synchrones laden der Werte
endmodule
