// Logisim project 8Bit_PC_V0.1.circ as structural Verilog: 16 circuits, main circuit main
module main (
);

  wire ABinv, ACin, button_1_out, button_2_out, clk, clk_halt, Disp_Load, EEParg, EEPladr, flipflop_1_q,
       flipflop_2_q, IRI, NOT_ALU_COUT_EO, NOT_ALU_EO, NOT_EEPEO, NOT_EEwrite, NOT_PCEO, NOT_PCL, NOT_RAEO,
       NOT_RAMEO, NOT_RAMwrite, NOT_RBEO, PCCE, RAMladr, RLA, RLB, zero;
  wire [7:0] ireg_1_out, ireg_2_out, ram_1_dout, REG_A, REG_B;

  FlipFlop flipflop_1 (.toggle(button_1_out), .Q(flipflop_1_q));
  Button button_1 (.out(button_1_out));
  Clock clock_1 (.ClkHalt(clk_halt), .ClkMan(flipflop_1_q), .Clk(clk));
  RAM ram_1 (.D_IN(ram_1_dout), .NOT_EO(NOT_RAMEO), .NOT_write(NOT_RAMwrite), .LoadAdr(RAMladr), .Dout(ram_1_dout));
  EEPROM eeprom_1 (
    .D_IN(ram_1_dout), .NOT_write(NOT_EEwrite), .args(EEParg), .LoadAdr(EEPladr), .NOT_EO(NOT_EEPEO),
    .data(ram_1_dout));
  // Probe on ram_1_dout
  // Probe on ram_1_dout
  IReg ireg_1 (.LE(IRI), .In(ram_1_dout), .Out(ireg_1_out));
  ControllLogic controlllogic_1 (
    .Clk(clk), .IREG(ireg_1_out), .halt_man(flipflop_2_q), .zero(zero), .halt(clk_halt), .Disp_I(Disp_Load),
    .NOT_PC_LOAD_I(NOT_PCL), .RAM_ADR_I(RAMladr), .EEPROM_ADR_I(EEPladr), .REG_A_I(RLA), .REG_B_I(RLB),
    .REG_INST_I(IRI), .NOT_RAM_WRITE_I(NOT_RAMwrite), .NOT_EEPROM_WRITE_I(NOT_EEwrite), .NOT_PC_O(NOT_PCEO),
    .NOT_RAM_O(NOT_RAMEO), .NOT_EEPROM_O(NOT_EEPEO), .NOT_REG_A_O(NOT_RAEO), .NOT_REG_B_O(NOT_RBEO),
    .NOT_ALU_O(NOT_ALU_EO), .NOT_ALU_COUT_O(NOT_ALU_COUT_EO), .PC_INC(PCCE), .ALU_Cin(ACin),
    .ALU_Binv(ABinv), .EEPROM_ARG(EEParg));  // open: out_21
  PC pc_1 (.LoadIn(ram_1_dout), .PC_INC(PCCE), .Clk(clk), .NOT_load(NOT_PCL), .NOT_OE(NOT_PCEO), .PCout(ram_1_dout));
  ALU alu_1 (
    .B(REG_B), .NOT_ALU_COUT_EO(NOT_ALU_COUT_EO), .NOT_ALU_EO(NOT_ALU_EO), .Binv(ABinv), .Cin(ACin),
    .A(REG_A), .Zero(zero), .out(ram_1_dout));
  Reg_AB reg_ab_1 (
    .LE_A(RLA), .LE_B(RLB), .In(ram_1_dout), .NOT_EOA(NOT_RAEO), .OUT_BUS_A(ram_1_dout), .OUT_CPU_A(REG_A),
    .OUT_CPU_B(REG_B));
  IReg ireg_2 (.LE(Disp_Load), .In(ram_1_dout), .Out(ireg_2_out));
  // Probe on ireg_2_out
  FlipFlop flipflop_2 (.toggle(button_2_out), .Q(flipflop_2_q));
  Button button_2 (.out(button_2_out));

  // Notes on the sheet:
  //   INPUT MODUL!
  //   Clock Halt Manual
endmodule

// Reg
module Reg_AB (
  input  NOT_EOA,
  input  LE_A,
  input  LE_B,
  input  [7:0] In,
  output [7:0] OUT_BUS_A,
  output [7:0] OUT_CPU_A,
  output [7:0] OUT_CPU_B
);

  DIP_74574 dip_74574_1 (
    .Q1(OUT_CPU_A[0]), .Q2(OUT_CPU_A[1]), .Q3(OUT_CPU_A[2]), .Q4(OUT_CPU_A[3]), .Q5(OUT_CPU_A[4]),
    .Q6(OUT_CPU_A[5]), .Q7(OUT_CPU_A[6]), .Q8(OUT_CPU_A[7]), .D1(In[0]), .D2(In[1]), .OE(1'b0), .D3(In[2]),
    .D4(In[3]), .D5(In[4]), .D6(In[5]), .D7(In[6]), .CLK(LE_A), .D8(In[7]));
  DIP_74574 dip_74574_2 (
    .Q1(OUT_CPU_B[0]), .Q2(OUT_CPU_B[1]), .Q3(OUT_CPU_B[2]), .Q4(OUT_CPU_B[3]), .Q5(OUT_CPU_B[4]),
    .Q6(OUT_CPU_B[5]), .Q7(OUT_CPU_B[6]), .Q8(OUT_CPU_B[7]), .D1(In[0]), .D2(In[1]), .OE(1'b0), .D3(In[2]),
    .D4(In[3]), .D5(In[4]), .D6(In[5]), .D7(In[6]), .CLK(LE_B), .D8(In[7]));
  LED IN_A_LED (.in(LE_A));
  LED IN_B_LED (.in(LE_B));
  // BusTranscever bustranscever_1: pin names not known; wires that end beside it: OUT_CPU_A, 1'b1, OUT_CPU_A, NOT_EOA, OUT_BUS_A
  Hex_Digit_Display A_HIGH (.value(OUT_CPU_A[7:4]));  // open: dp
  Hex_Digit_Display A_LOW (.value(OUT_CPU_A[3:0]));  // open: dp
  Hex_Digit_Display B_HIGH (.value(OUT_CPU_B[7:4]));  // open: dp
  Hex_Digit_Display B_LOW (.value(OUT_CPU_B[3:0]));  // open: dp
  LED OUT_LED (.in(NOT_EOA));
endmodule

module Display (
  input  [7:0] in_1
);

  Hex_Digit_Display hex_digit_display_1 (.value(in_1[3:0]), .dp(1'b0));
  Hex_Digit_Display hex_digit_display_2 (.value(in_1[7:4]), .dp(1'b0));
endmodule

module Clock (
  input  ClkHalt,
  input  ClkMan,
  output Clk
);

  wire and_1_out, clock_1_out, not_1_out;

  Clock_part clock_1 (.out(clock_1_out));
  and and_1 (and_1_out, clock_1_out, not_1_out);
  not not_1 (not_1_out, ClkHalt);
  or or_1 (Clk, and_1_out, ClkMan);
  LED led_1 (.in(Clk));
endmodule

module PC (
  input  Clk,
  input  NOT_load,
  input  NOT_OE,
  input  PC_INC,
  input  [7:0] LoadIn,
  output [7:0] PCout
);

  wire dip_74163_1_tc;
  wire [3:0] dip_74163_1_q1, dip_74163_2_q1;

  LED IN_LED (.in(NOT_load));
  LED OUT_LED (.in(NOT_OE));
  DIP_74163 dip_74163_1 (
    .Q1(dip_74163_1_q1[0]), .Q2(dip_74163_1_q1[1]), .Q3(dip_74163_1_q1[2]), .Q4(dip_74163_1_q1[3]),
    .TC(dip_74163_1_tc), .LE(NOT_load), .CEP(PC_INC), .CET(PC_INC), .CLK(Clk), .D1(LoadIn[0]),
    .D2(LoadIn[1]), .D3(LoadIn[2]), .CE(1'b0), .D4(LoadIn[3]));
  DIP_74163 dip_74163_2 (
    .Q1(dip_74163_2_q1[0]), .Q2(dip_74163_2_q1[1]), .Q3(dip_74163_2_q1[2]), .Q4(dip_74163_2_q1[3]),
    .LE(NOT_load), .CEP(dip_74163_1_tc), .CET(dip_74163_1_tc), .CLK(Clk), .D1(LoadIn[4]), .D2(LoadIn[5]),
    .D3(LoadIn[6]), .CE(1'b0), .D4(LoadIn[7]));  // open: TC
  Hex_Digit_Display B_HIGH (.value(dip_74163_2_q1));  // open: dp
  Hex_Digit_Display B_LOW (.value(dip_74163_1_q1));  // open: dp
  BusTranscever bustranscever_1 (
    .Ain({dip_74163_2_q1, dip_74163_1_q1}), .Bin(PCout), .dir(1'b1), .NOT_OE(NOT_OE),
    .A({dip_74163_2_q1, dip_74163_1_q1}), .B(PCout));

  // Other names for the same wires on the sheet: INC = PC_INC; NOT_EO = NOT_OE

  // Notes on the sheet:
  //   74163: https://www.ti.com/lit/ds/symlink/sn54ls161a.pdf?ts=1736241297246&ref_url=https%253A%252F%252Fwww.google.com%252F
endmodule

module RAM (
  input  LoadAdr,
  input  NOT_EO,
  input  NOT_write,
  input  [7:0] D_IN,
  output [7:0] Dout
);

  wire EO, write;
  wire [7:0] dip_74574_1_q1, ram_1_dout;

  not not_1 (write, NOT_write);
  DIP_74574 dip_74574_1 (
    .Q1(dip_74574_1_q1[0]), .Q2(dip_74574_1_q1[1]), .Q3(dip_74574_1_q1[2]), .Q4(dip_74574_1_q1[3]),
    .Q5(dip_74574_1_q1[4]), .Q6(dip_74574_1_q1[5]), .Q7(dip_74574_1_q1[6]), .Q8(dip_74574_1_q1[7]),
    .D1(D_IN[0]), .D2(D_IN[1]), .OE(1'b0), .D3(D_IN[2]), .D4(D_IN[3]), .D5(D_IN[4]), .D6(D_IN[5]),
    .D7(D_IN[6]), .CLK(LoadAdr), .D8(D_IN[7]));
  not not_2 (EO, NOT_EO);
  LED ADR_LED (.in(LoadAdr));
  LED WRITE_LED (.in(write));
  Hex_Digit_Display ADR_HIGH (.value(dip_74574_1_q1[7:4]));  // open: dp
  Hex_Digit_Display ADR_LOW (.value(dip_74574_1_q1[3:0]));  // open: dp
  RAM_part #(.trigger("high"), .\type ("nonvolatile")) ram_1 (
    .addr(dip_74574_1_q1), .we(write), .oe(1'b1), .din(D_IN), .dout(ram_1_dout));
  Hex_Digit_Display B_HIGH (.value(ram_1_dout[7:4]));  // open: dp
  Hex_Digit_Display B_LOW (.value(ram_1_dout[3:0]));  // open: dp
  LED #(.active("false")) OUT_LED (.in(NOT_EO));
  BusTranscever bustranscever_1 (.Ain(ram_1_dout), .Bin(Dout), .dir(1'b1), .NOT_OE(NOT_EO), .A(ram_1_dout), .B(Dout));

  // Other names for the same wires on the sheet: LE = LoadAdr; NEO = NOT_EO
endmodule

module EEPROM (
  input  LoadAdr,
  input  NOT_EO,
  input  NOT_write,
  input  args,
  input  [7:0] D_IN,
  output [7:0] data
);

  wire write;
  wire [3:0] multiplexer_1_out, ram_1_dout, ram_1_dout_2;
  wire [8:1] dip_74574_1_q1;

  DIP_74574 dip_74574_1 (
    .Q1(dip_74574_1_q1[1]), .Q2(dip_74574_1_q1[2]), .Q3(dip_74574_1_q1[3]), .Q4(dip_74574_1_q1[4]),
    .Q5(dip_74574_1_q1[5]), .Q6(dip_74574_1_q1[6]), .Q7(dip_74574_1_q1[7]), .Q8(dip_74574_1_q1[8]),
    .D1(D_IN[0]), .D2(D_IN[1]), .OE(1'b0), .D3(D_IN[2]), .D4(D_IN[3]), .D5(D_IN[4]), .D6(D_IN[5]),
    .D7(D_IN[6]), .CLK(LoadAdr), .D8(D_IN[7]));
  LED ADR_LED (.in(LoadAdr));
  not not_1 (write, NOT_write);
  Hex_Digit_Display HIGH (.value(dip_74574_1_q1[8:5]));  // open: dp
  LED WRITE_LED (.in(write));
  RAM_part #(.addrWidth(9), .trigger("high"), .\type ("nonvolatile")) ram_1 (
    .addr({dip_74574_1_q1, args}), .we(write), .oe(1'b1), .din(D_IN), .dout({ram_1_dout_2, ram_1_dout}));
  Hex_Digit_Display LOW (.value(dip_74574_1_q1[4:1]));  // open: dp
  Multiplexer #(.width(4)) multiplexer_1 (.in0(4'b0000), .in1(4'b1010), .out(multiplexer_1_out), .sel(args));
  Hex_Digit_Display ARG_DISP (.value(multiplexer_1_out));  // open: dp
  BusTranscever bustranscever_1 (
    .Ain({ram_1_dout_2, ram_1_dout}), .Bin(data), .dir(1'b1), .NOT_OE(NOT_EO),
    .A({ram_1_dout_2, ram_1_dout}), .B(data));
  Hex_Digit_Display OUT_HIGH (.value(ram_1_dout_2));  // open: dp
  Hex_Digit_Display OUT_LOW (.value(ram_1_dout));  // open: dp
  LED #(.active("false")) OUT_LED (.in(NOT_EO));

  // Other names for the same wires on the sheet: LE = LoadAdr; NEO = NOT_EO

  // Notes on the sheet:
  //   Args, der 2te speicherbereich für die Argumente der Befehle im ersten Speicherbereich
  //   Argument soll auf lsb, damit es hinter der Instruction steht
endmodule

module ALU_Old (
  input  Binv,
  input  [7:0] A,
  input  Cin,
  input  [7:0] B,
  output [7:0] Y,
  output Cout
);

  wire B0, B1, B2, B3, B4, B5, B6, B7, Carry;

  mdip_74283 mdip_74283_1 (
    .B1(B0), .A2(B1), .CIN(Cin), .B2(A[1]), .A3(A[2]), .B3(B2), .A4(B3), .B4(A[3]), .A1(A[0]), .Y2(Y[1]),
    .Y3(Y[2]), .Y1(Y[0]), .Y4(Y[3]), .COUT(Carry));
  mdip_74283 mdip_74283_2 (
    .B1(B4), .A2(B5), .CIN(Carry), .B2(A[5]), .A3(A[6]), .B3(B6), .A4(B7), .B4(A[7]), .A1(A[4]), .Y2(Y[5]),
    .Y3(Y[6]), .Y1(Y[4]), .Y4(Y[7]), .COUT(Cout));
  DIP_7486 dip_7486_1 (
    .Y2(B1), .Y3(B2), .Y4(B3), .Y1(B0), .A2(Binv), .B2(B[1]), .A3(Binv), .A1(Binv), .B3(B[2]), .A4(Binv),
    .B4(B[3]), .B1(B[0]));
  DIP_7486 dip_7486_2 (
    .Y2(B5), .Y3(B6), .Y4(B7), .Y1(B4), .A2(Binv), .B2(B[5]), .A3(Binv), .A1(Binv), .B3(B[6]), .A4(Binv),
    .B4(B[7]), .B1(B[4]));

  // Other names for the same wires on the sheet: rB0 = B[0]; rB1 = B[1]; rB2 = B[2]; rB3 = B[3]; rB4 = B[4];
  //   rB5 = B[5]; rB6 = B[6]; rB7 = B[7]
endmodule

// 74LS245
module L_74_245 (
  input  Dir,
  input  NOT_OE_5a23fa50,
  input  A1,
  input  in_4,
  input  in_5,
  input  in_6,
  input  A3,
  input  B3,
  input  A4,
  input  B4,
  input  A5,
  input  B5,
  input  in_13,
  input  B6,
  input  A7,
  input  B7,
  input  in_17,
  input  B8,
  output B1,
  output out_20,
  output B2,
  output A2,
  output out_23,
  output out_24,
  output out_25,
  output out_26,
  output out_27,
  output out_28,
  output out_29,
  output A6,
  output out_31,
  output out_32,
  output out_33,
  output A8
);

  wire and_1_out, and_2_out;

  and and_1 (and_1_out, Dir, ~NOT_OE_5a23fa50);  // AND_Gate
  assign B1 = and_1_out ? A1 : 1'bz;  // Controlled_Buffer controlled_buffer_1
  assign B2 = and_1_out ? in_5 : 1'bz;  // Controlled_Buffer controlled_buffer_2
  assign out_23 = and_1_out ? A3 : 1'bz;  // Controlled_Buffer controlled_buffer_3
  assign out_25 = and_1_out ? A4 : 1'bz;  // Controlled_Buffer controlled_buffer_4
  assign out_27 = and_1_out ? A5 : 1'bz;  // Controlled_Buffer controlled_buffer_5
  assign out_29 = and_1_out ? in_13 : 1'bz;  // Controlled_Buffer controlled_buffer_6
  assign out_31 = and_1_out ? A7 : 1'bz;  // Controlled_Buffer controlled_buffer_7
  assign out_33 = and_1_out ? in_17 : 1'bz;  // Controlled_Buffer controlled_buffer_8
  and and_2 (and_2_out, ~Dir, ~NOT_OE_5a23fa50);  // AND_Gate
  assign out_20 = and_2_out ? in_4 : 1'bz;  // Controlled_Buffer controlled_buffer_9
  assign A2 = and_2_out ? in_6 : 1'bz;  // Controlled_Buffer controlled_buffer_10
  assign out_24 = and_2_out ? B3 : 1'bz;  // Controlled_Buffer controlled_buffer_11
  assign out_26 = and_2_out ? B4 : 1'bz;  // Controlled_Buffer controlled_buffer_12
  assign out_28 = and_2_out ? B5 : 1'bz;  // Controlled_Buffer controlled_buffer_13
  assign A6 = and_2_out ? B6 : 1'bz;  // Controlled_Buffer controlled_buffer_14
  assign out_32 = and_2_out ? B7 : 1'bz;  // Controlled_Buffer controlled_buffer_15
  assign A8 = and_2_out ? B8 : 1'bz;  // Controlled_Buffer controlled_buffer_16
endmodule

// 245_BT
module BusTranscever (
  input  NOT_OE,
  input  dir,
  input  [7:0] Ain,
  input  [7:0] Bin,
  output [7:0] A,
  output [7:0] B
);

  wire DIR_AND_NOE, NDIR_AND_NOE, NOT_dir, OE;
  wire [7:0] controlled_buffer_1_out, l_74_245_1_b1;

  not not_1 (OE, NOT_OE);
  not not_2 (NOT_dir, dir);
  assign controlled_buffer_1_out = dir ? Ain : 8'bz;  // Controlled_Buffer controlled_buffer_1
  assign A = DIR_AND_NOE ? controlled_buffer_1_out : 8'bz;  // Controlled_Buffer controlled_buffer_2
  L_74_245 l_74_245_1 (
    .Dir(dir), .A1(controlled_buffer_1_out[0]), .in_5(controlled_buffer_1_out[1]),
    .A3(controlled_buffer_1_out[2]), .A4(controlled_buffer_1_out[3]), .A5(controlled_buffer_1_out[4]),
    .in_13(controlled_buffer_1_out[5]), .A7(controlled_buffer_1_out[6]), .in_17(controlled_buffer_1_out[7]),
    .NOT_OE_5a23fa50(NOT_OE), .in_4(l_74_245_1_b1[0]), .in_6(l_74_245_1_b1[1]), .B3(l_74_245_1_b1[2]),
    .B4(l_74_245_1_b1[3]), .B5(l_74_245_1_b1[4]), .B6(l_74_245_1_b1[5]), .B7(l_74_245_1_b1[6]),
    .B8(l_74_245_1_b1[7]), .out_20(controlled_buffer_1_out[0]), .A2(controlled_buffer_1_out[1]),
    .out_24(controlled_buffer_1_out[2]), .out_26(controlled_buffer_1_out[3]),
    .out_28(controlled_buffer_1_out[4]), .A6(controlled_buffer_1_out[5]),
    .out_32(controlled_buffer_1_out[6]), .A8(controlled_buffer_1_out[7]), .B1(l_74_245_1_b1[0]),
    .B2(l_74_245_1_b1[1]), .out_23(l_74_245_1_b1[2]), .out_25(l_74_245_1_b1[3]), .out_27(l_74_245_1_b1[4]),
    .out_29(l_74_245_1_b1[5]), .out_31(l_74_245_1_b1[6]), .out_33(l_74_245_1_b1[7]));
  and and_1 (NDIR_AND_NOE, OE, dir);
  and and_2 (DIR_AND_NOE, OE, NOT_dir);
  assign l_74_245_1_b1 = NOT_dir ? Bin : 8'bz;  // Controlled_Buffer controlled_buffer_3
  assign B = NDIR_AND_NOE ? l_74_245_1_b1 : 8'bz;  // Controlled_Buffer controlled_buffer_4
endmodule

module ALU (
  input  [7:0] A,
  input  [7:0] B,
  input  Binv,
  input  Cin,
  input  NOT_ALU_COUT_EO,
  input  NOT_ALU_EO,
  output [7:0] out,
  output Zero
);

  wire B0, B1, B2, B3, B4, B5, B6, B7, Carry, Cout, Cout_EO, dip_7402_1_y1, dip_7402_1_y2, dip_7402_1_y3,
       dip_7402_1_y4, dip_7408_1_y1, dip_7408_1_y4, Y0, Y1, Y2, Y3, Y4, Y5, Y6, Y7;
  wire [6:0] bustranscever_1_a;
  wire [7:0] multiplexer_1_out;

  mdip_74283 mdip_74283_1 (
    .B1(B0), .A2(B1), .CIN(Cin), .B2(A[1]), .A3(A[2]), .B3(B2), .A4(B3), .B4(A[3]), .A1(A[0]), .Y2(Y1),
    .Y3(Y2), .Y1(Y0), .Y4(Y3), .COUT(Carry));
  mdip_74283 mdip_74283_2 (
    .B1(B4), .A2(B5), .CIN(Carry), .B2(A[5]), .A3(A[6]), .B3(B6), .A4(B7), .B4(A[7]), .A1(A[4]), .Y2(Y5),
    .Y3(Y6), .Y1(Y4), .Y4(Y7), .COUT(Cout));
  DIP_7486 dip_7486_1 (
    .Y2(B1), .Y3(B2), .Y4(B3), .Y1(B0), .A2(Binv), .B2(B[1]), .A3(Binv), .A1(Binv), .B3(B[2]), .A4(Binv),
    .B4(B[3]), .B1(B[0]));
  DIP_7486 dip_7486_2 (
    .Y2(B5), .Y3(B6), .Y4(B7), .Y1(B4), .A2(Binv), .B2(B[5]), .A3(Binv), .A1(Binv), .B3(B[6]), .A4(Binv),
    .B4(B[7]), .B1(B[4]));
  Multiplexer #(.width(8)) multiplexer_1 (
    .in0({Y7, Y6, Y5, Y4, Y3, Y2, Y1, Y0}), .in1({bustranscever_1_a, Cout}), .out(multiplexer_1_out),
    .sel(Cout_EO));
  DIP_7402 dip_7402_1 (
    .Y2(dip_7402_1_y2), .Y3(dip_7402_1_y3), .Y4(dip_7402_1_y4), .Y1(dip_7402_1_y1), .A2(Y3), .B2(Y2),
    .A3(Y4), .A1(Y0), .B3(Y5), .A4(Y6), .B4(Y7), .B1(Y1));
  DIP_7408 dip_7408_1 (
    .Y2(Zero), .Y4(dip_7408_1_y4), .Y1(dip_7408_1_y1), .A2(dip_7408_1_y1), .B2(dip_7408_1_y4),
    .A1(dip_7402_1_y4), .A4(dip_7402_1_y2), .B4(dip_7402_1_y1), .B1(dip_7402_1_y3));  // open: Y3, A3, B3
  Hex_Digit_Display HIGH (.value(multiplexer_1_out[7:4]));  // open: dp
  Hex_Digit_Display LOW (.value(multiplexer_1_out[3:0]));  // open: dp
  BusTranscever bustranscever_1 (
    .Ain({bustranscever_1_a, Cout}), .Bin(out), .dir(1'b1), .NOT_OE(NOT_ALU_COUT_EO),
    .A({bustranscever_1_a, Cout}), .B(out));
  BusTranscever bustranscever_2 (
    .Ain({Y7, Y6, Y5, Y4, Y3, Y2, Y1, Y0}), .Bin(out), .dir(1'b1), .NOT_OE(NOT_ALU_EO),
    .A({Y7, Y6, Y5, Y4, Y3, Y2, Y1, Y0}), .B(out));
  not not_1 (Cout_EO, NOT_ALU_COUT_EO);
  LED OUT_COUT_LED (.in(NOT_ALU_COUT_EO));
  LED OUT_LED (.in(NOT_ALU_EO));
  // also tied to GND on the sheet: {bustranscever_1_a[0], bustranscever_1_a[1], bustranscever_1_a[2], bustranscever_1_a[3], bustranscever_1_a[4], bustranscever_1_a[5], bustranscever_1_a[6]}

  // Other names for the same wires on the sheet: rB0 = B[0]; rB1 = B[1]; rB2 = B[2]; rB3 = B[3]; rB4 = B[4];
  //   rB5 = B[5]; rB6 = B[6]; rB7 = B[7]

  // Notes on the sheet:
  //   B <= A == Cout when Binv & Cin 
  //   Dont Forget Resistors for short circuit protection
endmodule

// T-FF
module FlipFlop (
  input  toggle,
  output Q
);

  J_K_Flip_Flop j_k_ff_1 (.J(toggle), .K(toggle), .clk(toggle), .Q(Q));  // open: Qn, preset, reset
endmodule

module InstReg (
  input  NOT_OE_5a23fa50,
  input  LE,
  input  [7:0] In,
  output [7:0] Out_A_d614a9c4
);

  DIP_74574 dip_74574_1 (
    .Q1(Out_A_d614a9c4[0]), .Q2(Out_A_d614a9c4[1]), .Q3(Out_A_d614a9c4[2]), .Q4(Out_A_d614a9c4[3]),
    .Q5(Out_A_d614a9c4[4]), .Q6(Out_A_d614a9c4[5]), .Q7(Out_A_d614a9c4[6]), .Q8(Out_A_d614a9c4[7]),
    .D1(In[0]), .D2(In[1]), .OE(NOT_OE_5a23fa50), .D3(In[2]), .D4(In[3]), .D5(In[4]), .D6(In[5]), .D7(In[6]),
    .CLK(LE), .D8(In[7]));
endmodule

// IREG
module IReg (
  input  LE,
  input  [7:0] In,
  output [7:0] Out
);

  DIP_74574 dip_74574_1 (
    .Q1(Out[0]), .Q2(Out[1]), .Q3(Out[2]), .Q4(Out[3]), .Q5(Out[4]), .Q6(Out[5]), .Q7(Out[6]), .Q8(Out[7]),
    .D1(In[0]), .D2(In[1]), .OE(1'b0), .D3(In[2]), .D4(In[3]), .D5(In[4]), .D6(In[5]), .D7(In[6]), .CLK(LE),
    .D8(In[7]));
  Hex_Digit_Display B_HIGH (.value(Out[7:4]));  // open: dp
  Hex_Digit_Display B_LOW (.value(Out[3:0]));  // open: dp

  // Notes on the sheet:
  //   Durchlässiger 573er für register unbrauchbar, muss 574 sein, getakted
endmodule

// Instruction Logic
module ControllLogic (
  input  zero,
  input  Clk,
  input  [7:0] IREG,
  input  halt_man,
  output NOT_PC_LOAD_I,
  output RAM_ADR_I,
  output EEPROM_ADR_I,
  output REG_A_I,
  output REG_B_I,
  output REG_INST_I,
  output NOT_RAM_WRITE_I,
  output NOT_PC_O,
  output NOT_EEPROM_WRITE_I,
  output NOT_RAM_O,
  output NOT_EEPROM_O,
  output NOT_REG_A_O,
  output NOT_REG_B_O,
  output NOT_ALU_O,
  output halt,
  output NOT_ALU_COUT_O,
  output out_21,
  output PC_INC,
  output ALU_Cin,
  output ALU_Binv,
  output EEPROM_ARG,
  output Disp_I
);

  wire dip_7408_2_y2, dip_74138_1_y1, dip_74138_1_y2, dip_74138_1_y3, dip_74138_1_y4, dip_74138_1_y5,
       dispI_I, EEPAI_I, EEPWI_I, halt_soft, JUMP_I2, not_6_out, not_7_out, PCLI_I, RAMAI_I, RAMWI_I,
       REGAI_I, REGBI_I, REGII_I;
  wire [3:0] I_MEM_ADD;
  wire [7:0] H_Inst;
  wire [7:4] IndipendentSig;

  DIP_74163 dip_74163_1 (
    .Q1(I_MEM_ADD[0]), .Q2(I_MEM_ADD[1]), .Q3(I_MEM_ADD[2]), .Q4(I_MEM_ADD[3]), .LE(1'b1), .CEP(1'b1),
    .CET(1'b1), .CLK(Clk), .D1(1'b0), .D2(1'b0), .D3(1'b0), .CE(IndipendentSig[7]), .D4(1'b0));  // open: TC
  DIP_74138 dip_74138_1 (
    .Y0(PCLI_I), .Y1(dip_74138_1_y1), .Y2(dip_74138_1_y2), .Y3(dip_74138_1_y3), .Y4(dip_74138_1_y4),
    .Y5(dip_74138_1_y5), .Y6(RAMWI_I), .Y7(EEPWI_I), .A0(H_Inst[4]), .A1(H_Inst[5]), .OE1(1'b0), .in_5(1'b0),
    .OE2(H_Inst[7]), .A2(H_Inst[6]));
  DIP_74138 dip_74138_2 (
    .Y0(NOT_PC_O), .Y1(NOT_RAM_O), .Y2(NOT_EEPROM_O), .Y3(NOT_REG_A_O), .Y4(NOT_REG_B_O), .Y5(NOT_ALU_O),
    .Y6(NOT_ALU_COUT_O), .Y7(out_21), .A0(H_Inst[0]), .A1(H_Inst[1]), .OE1(1'b0), .in_5(1'b0),
    .OE2(H_Inst[3]), .A2(H_Inst[2]));
  not not_1 (RAMAI_I, dip_74138_1_y1);
  not not_2 (EEPAI_I, dip_74138_1_y2);
  not not_3 (REGAI_I, dip_74138_1_y3);
  not not_4 (REGBI_I, dip_74138_1_y4);
  not not_5 (REGII_I, dip_74138_1_y5);
  ROM #(.addrWidth(12)) rom_1 (.addr({IREG, I_MEM_ADD}), .data(H_Inst));
  not not_6 (not_6_out, JUMP_I2);
  DIP_7408 dip_7408_1 (
    .Y2(EEPROM_ADR_I), .Y3(REG_B_I), .Y4(REG_A_I), .Y1(RAM_ADR_I), .A2(Clk), .B2(EEPAI_I), .A3(Clk),
    .A1(Clk), .B3(REGBI_I), .A4(REGAI_I), .B4(Clk), .B1(RAMAI_I));
  DIP_7408 dip_7408_2 (
    .Y2(dip_7408_2_y2), .Y3(JUMP_I2), .Y4(Disp_I), .Y1(REG_INST_I), .A2(PCLI_I), .B2(not_6_out), .A3(zero),
    .A1(Clk), .B3(IndipendentSig[4]), .A4(dispI_I), .B4(Clk), .B1(REGII_I));
  not not_7 (not_7_out, Clk);
  DIP_7432 dip_7432_1 (
    .Y2(NOT_RAM_WRITE_I), .Y3(halt), .Y4(NOT_EEPROM_WRITE_I), .Y1(NOT_PC_LOAD_I), .A2(not_7_out),
    .B2(RAMWI_I), .A3(halt_soft), .A1(not_7_out), .B3(halt_man), .A4(EEPWI_I), .B4(not_7_out),
    .B1(dip_7408_2_y2));
  ROM #(.addrWidth(12)) rom_2 (
    .addr({IREG, I_MEM_ADD}),
    .data({IndipendentSig[7], halt_soft, dispI_I, IndipendentSig[4], EEPROM_ARG, ALU_Binv, ALU_Cin, PC_INC}));

  // Other names for the same wires on the sheet: EEPAI = EEPROM_ADR_I; EEPWI = NOT_EEPROM_WRITE_I;
  //   out_Enable = H_Inst[3]; in_Enable = H_Inst[7]; Istep[3:0] = I_MEM_ADD; I_MEM_ADD[11:4] = IREG; Iadr[7:0] = IREG;
  //   IndipendentSig (some bits) = {halt_soft, dispI_I, EEPROM_ARG, ALU_Binv, ALU_Cin, PC_INC};
  //   L_Inst[7:0] = {IndipendentSig[7], halt_soft, dispI_I, IndipendentSig[4], EEPROM_ARG, ALU_Binv, ALU_Cin, PC_INC};
  //   jump_I = IndipendentSig[4]; stepReset = IndipendentSig[7]; inSignalsDec[2:0] = H_Inst[6:4];
  //   outSignalsDec[2:0] = H_Inst[2:0]; PCLI = NOT_PC_LOAD_I; RAMAI = RAM_ADR_I; RAMWI = NOT_RAM_WRITE_I;
  //   REGAI = REG_A_I; REGBI = REG_B_I; REGII = REG_INST_I

  // Notes on the sheet:
  //   Doppelt so viele outputs -1 möglich mit 2. 138 und out Enable signal als mux
  //   OUTPUT
  //   8
  //   9
  //   a
  //   b
  //   c
  //   d
  //   f
  //   Noch Zwei Outputs Frei zum Anbringen
  //   contents of rom_1 (hex, n*v repeats v):
  //   a8 da 14*0 a8 da 9a ed 12*0 a8 da 9a ed 12*0 a8 da 9a b9 12*0 a8 da 9a c9 12*0 a8 da 8a 13*0 a8 da
  //   9a 9 12*0 a8 da 9a 13*0 a8 da ea 13*0 a8 da 9a 9 12*0 a8 da 14*0 a8 da ba 13*0 a8 da ca 13*0 a8 da
  //   9a eb 12*0 a8 da a
  //   e
  //   Eingabe vllt ?
  //   IO Rom
  //   Clock, für synchrones laden der Werte
  //   not_Jmp
  //   Clock Halt
  //   Führt zu PCLI
  //   contents of rom_2 (hex, n*v repeats v):
  //   0 0 81 15*0 8 0 81 13*0 8 6 81 13*0 8 0 81 13*0 8 0 81 13*0 8 81 14*0 8 16 81 13*0 8 81 14*0 8 81
  //   14*0 8 20 81 13*0 40 81 14*0 8 81 14*0 8 81 14*0 8 0 81 13*0 1e 81
  //   1
  //   2
  //   4
  //   Special Instruction Rom
  //   8
  //   10
  //   80
  //   20
  //   INPUT
  //   NC zu Clock Halt
  //   40
endmodule

// 74283
module mdip_74283 (
  input  CIN,
  input  A1,
  input  B1,
  input  A2,
  input  B2,
  input  A3,
  input  B3,
  input  A4,
  input  B4,
  output Y1,
  output Y2,
  output Y3,
  output Y4,
  output COUT
);

  wire and_1_out, and_2_out, and_3_out, and_4_out, and_5_out, and_6_out, and_7_out, and_8_out, and_9_out,
       and_10_out, and_11_out, and_12_out, and_13_out, and_14_out, nand_1_out, nand_2_out, nand_3_out,
       nand_4_out, nor_1_out, nor_2_out, nor_3_out, nor_4_out, nor_5_out, nor_6_out, nor_7_out, not_1_out,
       not_2_out, not_3_out, not_4_out, not_5_out, not_6_out;

  not not_1 (not_1_out, CIN);
  nor nor_1 (nor_1_out, A1, B1);
  nand nand_1 (nand_1_out, A1, B1);
  nor nor_2 (nor_2_out, A2, B2);
  nand nand_2 (nand_2_out, A2, B2);
  nor nor_3 (nor_3_out, A3, B3);
  nand nand_3 (nand_3_out, A3, B3);
  nor nor_4 (nor_4_out, A4, B4);
  nand nand_4 (nand_4_out, A4, B4);
  not not_2 (not_2_out, not_1_out);
  not not_3 (not_3_out, nor_1_out);
  and and_1 (and_1_out, not_1_out, nand_1_out);
  not not_4 (not_4_out, nor_2_out);
  and and_2 (and_2_out, not_1_out, nand_1_out, nand_2_out);
  and and_3 (and_3_out, nand_2_out, nor_1_out);
  not not_5 (not_5_out, nor_3_out);
  and and_4 (and_4_out, not_1_out, nand_1_out, nand_2_out, nand_3_out);
  and and_5 (and_5_out, nand_2_out, nand_3_out, nor_1_out);
  and and_6 (and_6_out, nand_3_out, nor_2_out);
  not not_6 (not_6_out, nor_4_out);
  and and_7 (and_7_out, not_1_out, nand_1_out, nand_2_out, nand_3_out, nand_4_out);
  and and_8 (and_8_out, nand_2_out, nand_3_out, nand_4_out, nor_1_out);
  and and_9 (and_9_out, nand_3_out, nand_4_out, nor_2_out);
  and and_10 (and_10_out, nand_4_out, nor_3_out);
  and and_11 (and_11_out, not_3_out, nand_1_out);
  nor nor_5 (nor_5_out, and_1_out, nor_1_out);
  and and_12 (and_12_out, not_4_out, nand_2_out);
  nor nor_6 (nor_6_out, and_2_out, and_3_out, nor_2_out);
  and and_13 (and_13_out, not_5_out, nand_3_out);
  nor nor_7 (nor_7_out, and_4_out, and_5_out, and_6_out, nor_3_out);
  and and_14 (and_14_out, not_6_out, nand_4_out);
  nor nor_8 (COUT, and_7_out, and_8_out, and_9_out, and_10_out, nor_4_out);
  xor xor_1 (Y1, not_2_out, and_11_out);
  xor xor_2 (Y2, nor_5_out, and_12_out);
  xor xor_3 (Y3, nor_6_out, and_13_out);
  xor xor_4 (Y4, nor_7_out, and_14_out);
endmodule
